# Fritzing sketch ArduinoBoostConverter (saved by Fritzing 0.9.1b)
circuit board: 8.46667cm x 5.64444cm
breadboards: 1

parts:
  Bauteil1 = Arduino Uno (Rev3)
  Q1 = NPN-Transistor [package="TO92 [THT]"]
  R1 = Resistor [tolerance=±5% resistance=1k package=THT]
  R2 = Resistor [tolerance=±5% resistance=150k package=THT]
  R3 = Resistor [tolerance=±5% resistance=10k package=THT]
  L1 = Inductor [inductance=330µH package="400 mil [THT]"]
  R4 = Resistor [tolerance=±5% resistance=2.2k package=THT]
  LED1 = LED - 5mm [color="Green (555nm)" package="5 mm [THT]"]
  C1 = Electrolytic Capacitor [capacitance=47µF voltage=50V package="100 mil [THT, electrolytic]"]
  D1 = Rectifier Diode [part_number=1N4001 package="300 mil [THT]"]
  C2 = Ceramic Capacitor [capacitance=100nF voltage=50V package="100 mil [THT, multilayer]"]

nets:
  N1: Bauteil1.A0, R2.Pin_0, R3.Pin_0, C2.1
  N2: Bauteil1.GND, Q1.C, R3.Pin_1, LED1.cathode, C1.-, C2.0
  N3: Bauteil1.D6_PWM, R1.Pin_1
  N4: Bauteil1.5V, L1.pin_0
  N5: Q1.E, L1.pin_1, D1.anode
  N6: Q1.B, R1.Pin_0
  N7: R2.Pin_1, R4.Pin_0, C1.+, D1.cathode
  N8: R4.Pin_1, LED1.anode
